// Logisim project 6502.circ as structural Verilog: 4 circuits, main circuit main
module main (
);

  wire clock_1_out, clock_generator_1_phi1, clock_generator_1_phi2;

  Clock clock_1 (.out(clock_1_out));
  Clock_Generator clock_generator_1 (.clk0(clock_1_out), .phi1(clock_generator_1_phi1), .phi2(clock_generator_1_phi2));
endmodule

module _6502 (
  input  in_1,
  input  in_2,
  input  in_3,
  input  in_4,
  input  in_5,
  input  in_6,
  input  in_7,
  input  in_8,
  input  in_9,
  input  [7:0] in_10,
  input  in_11,
  input  in_12,
  input  in_13,
  input  in_14,
  output [7:0] out_15,
  output [7:0] out_16,
  output [7:0] out_17,
  output [15:0] out_18
);

  wire [7:0] AC_q, controlled_buffer_3_out, DOR_q, IDL_q, PCH_q, PCL_q, pull_resistor_1_node,
       pull_resistor_2_node, pull_resistor_3_node, pull_resistor_4_node, S_q, X_q, Y_q;

  Pull_Resistor #(.pull(1)) pull_resistor_1 (.node(pull_resistor_1_node));
  assign out_15 = in_1 ? pull_resistor_1_node : 8'bz;  // Controlled_Buffer controlled_buffer_1
  Pull_Resistor #(.pull(1)) pull_resistor_2 (.node(pull_resistor_2_node));
  assign out_17 = in_1 ? pull_resistor_2_node : 8'bz;  // Controlled_Buffer controlled_buffer_2
  Register #(.trigger("high")) ABL (.D(out_17), .en(in_11), .Q(out_18[7:0]), .clk(in_11));  // open: clr
  Register #(.trigger("high")) ABH (.D(controlled_buffer_3_out), .Q(out_18[15:8]));  // open: en, clk, clr
  Pull_Resistor #(.pull(1)) pull_resistor_3 (.node(pull_resistor_3_node));
  assign controlled_buffer_3_out = in_1 ? pull_resistor_3_node : 8'bz;  // Controlled_Buffer controlled_buffer_3
  assign out_15 = in_4 ? Y_q : 8'bz;  // Controlled_Buffer controlled_buffer_4
  Register #(.trigger("high")) Y (.D(out_15), .en(in_3), .Q(Y_q));  // open: clk, clr
  assign out_15 = in_6 ? X_q : 8'bz;  // Controlled_Buffer controlled_buffer_5
  Register #(.trigger("high")) X (.D(out_15), .en(in_5), .Q(X_q));  // open: clk, clr
  assign out_15 = in_7 ? S_q : 8'bz;  // Controlled_Buffer controlled_buffer_6
  Register #(.trigger("high")) S (.D(out_15), .Q(S_q));  // open: en, clk, clr
  Register #(.trigger("high")) ALUA ();  // open: D, en, Q, clk, clr
  Register #(.trigger("high")) ALUB ();  // open: D, en, Q, clk, clr
  Register #(.trigger("high")) ALU ();  // open: D, en, Q, clk, clr
  assign out_15 = in_1 ? pull_resistor_4_node : 8'bz;  // Controlled_Buffer controlled_buffer_7
  Pull_Resistor #(.pull(1)) pull_resistor_4 (.node(pull_resistor_4_node));
  assign out_15 = in_8 ? AC_q : 8'bz;  // Controlled_Buffer controlled_buffer_8
  Register #(.trigger("high")) AC (.D(out_15), .Q(AC_q));  // open: en, clk, clr
  assign out_17 = in_9 ? PCL_q : 8'bz;  // Controlled_Buffer controlled_buffer_9
  Register #(.trigger("high")) PCH (.Q(PCH_q));  // open: D, en, clk, clr
  Register #(.trigger("high")) PCL (.Q(PCL_q));  // open: D, en, clk, clr
  assign out_17 = in_12 ? IDL_q : 8'bz;  // Controlled_Buffer controlled_buffer_10
  assign controlled_buffer_3_out = in_13 ? PCH_q : 8'bz;  // Controlled_Buffer controlled_buffer_11
  assign controlled_buffer_3_out = in_14 ? IDL_q : 8'bz;  // Controlled_Buffer controlled_buffer_12
  Register #(.trigger("high")) DOR (.D(out_15), .Q(DOR_q));  // open: en, clk, clr
  Register #(.trigger("high")) IDL (.D(in_10), .Q(IDL_q));  // open: en, clk, clr
  assign out_16 = in_2 ? DOR_q : 8'bz;  // Controlled_Buffer controlled_buffer_13
endmodule

module PLA (
  input  t5,
  input  t4,
  input  t3,
  input  t2,
  input  [7:0] IR,
  input  clock1,
  input  clock2,
  output out_8,
  output out_9,
  output out_10,
  output out_11,
  output out_12,
  output out_13,
  output out_14,
  output out_15,
  output out_16,
  output out_17,
  output out_18,
  output out_19,
  output out_20
);

  wire nor_14_out, nor_15_out;

  nor nor_1 (out_8, IR[6], ~IR[2], ~IR[7], IR[5], nor_15_out);  // NOR_Gate
  nor nor_2 (out_9, ~IR[4], ~IR[0], t3, IR[3], IR[2]);  // NOR_Gate
  nor nor_3 (out_10, ~IR[4], ~IR[0], t2, ~IR[3], IR[2]);  // NOR_Gate
  nor nor_4 (out_11, clock1, IR[4], ~IR[7], ~IR[3], IR[5], nor_15_out, IR[2]);  // NOR_Gate
  nor nor_5 (out_12, clock1, IR[6], ~IR[7], ~IR[4], ~IR[3], IR[5], nor_15_out, IR[2]);  // NOR_Gate
  nor nor_6 (out_13, clock1, IR[4], ~IR[7], ~IR[6], IR[5], nor_15_out);  // NOR_Gate
  nor nor_7 (out_14, ~IR[2], ~IR[4], t2);  // NOR_Gate
  nor nor_8 (out_15, IR[6], ~IR[7], ~IR[1]);  // NOR_Gate
  nor nor_9 (out_16, IR[4], ~IR[0], t2, IR[3], IR[2]);  // NOR_Gate
  nor nor_10 (out_17, clock1, IR[6], IR[4], ~IR[7], ~IR[1], ~IR[3], IR[5], IR[2]);  // NOR_Gate
  nor nor_11 (out_18, clock1, IR[4], ~IR[7], ~IR[1], ~IR[6], ~IR[3], IR[5], IR[2]);  // NOR_Gate
  nor nor_12 (out_19, clock1, IR[4], ~IR[7], ~IR[6], nor_15_out, ~IR[5]);  // NOR_Gate
  nor nor_13 (out_20, IR[6], ~IR[7], ~IR[1], IR[5]);  // NOR_Gate
  not nor_14 (nor_14_out, clock1);  // NOR_Gate
  nor nor_15 (nor_15_out, IR[0], IR[1]);
endmodule

module Clock_Generator (
  input  clk0,
  output phi1,
  output phi2
);

  not not_1 (phi1, clk0);

  assign phi2 = clk0;
endmodule
